# Fritzing sketch pcb002 (saved by Fritzing 0.9.9b)
circuit board: 2.97573cm x 4.24617cm
breadboards: 1

parts:
  Arduino_Pro_Mini_5v = Arduino Pro Mini (3.3V)
  5v_IN = USB Connectors [package=usb-minib]  # not connected
  AHT20 = female pin header, 4 pins [form="♀ (female)"]
  LCD = female pin header, 3 pins [form="♀ (female)"]
  R1 = Resistor [tolerance=±5% power=0.25 resistance=220 package=THT]
  LED1 = LED - 5mm [color="Red (633nm)" current=0.030 package="5 mm [THT]"]
  Relay = female pin header, 2 pins [form="♀ (female)"]
  openLog = female pin header, 6 pins [form="♀ (female)"]

nets:
  N1: Arduino_Pro_Mini_5v.VCC, AHT20.pin1, LCD.pin1, openLog.pin4
  N2: Arduino_Pro_Mini_5v.A4, AHT20.pin3
  N3: Arduino_Pro_Mini_5v.A5, AHT20.pin2
  N4: Arduino_Pro_Mini_5v.MISO, openLog.pin3
  N5: Arduino_Pro_Mini_5v.MOSI, openLog.pin2
  N6: Arduino_Pro_Mini_5v.D10, openLog.pin1
  N7: Arduino_Pro_Mini_5v.D8, R1.Pin_0, Relay.pin1
  N8: Arduino_Pro_Mini_5v.D5, LCD.pin2
  N9: R1.Pin_1, LED1.anode

notes:
  VCC
  SCL
  SDA
  GRD
  OpenLog
