# Fritzing sketch pcb004 (saved by Fritzing 0.9.9b)
circuit board: 3.02058cm x 3.77498cm
breadboards: 1

parts:
  I2C = female pin header, 4 pins [form="♀ (female)"]
  R1 = Resistor [tolerance=±5% power=0.25 resistance=220 package=THT]
  LED1 = LED - 5mm [color="Red (633nm)" current=0.030 package="5 mm [THT]"]
  Relay = female pin header, 2 pins [form="♀ (female)"]
  J2 = female pin header, 4 pins [form="♀ (female)"]
  J4 = female pin header, 2 pins [form="♀ (female)"]  # not connected
  J5 = female pin header, 2 pins [form="♀ (female)"]
  Part1 = Arduino Pro Mini (5V)  # not connected
  USB_Breakout = female pin header, 5 pins [form="♀ (female)"]
  J3 = female pin header, 4 pins [form="♀ (female)"]
  I2C_2 = female pin header, 3 pins [form="♀ (female)"]
  I2C1 = female pin header, 4 pins [form="♀ (female)"]
  J1 = female pin header, 4 pins [form="♀ (female)"]  # not connected

nets:
  N1: I2C.pin1, J2.pin4, USB_Breakout.pin5, I2C_2.pin1, I2C1.pin1
  N2: I2C.pin2, J5.pin1, I2C1.pin2
  N3: I2C.pin3, J5.pin2, I2C1.pin3
  N4: R1.Pin_0, Relay.pin1, J3.pin2
  N5: R1.Pin_1, LED1.anode
  N6: J3.pin1, I2C_2.pin2

notes:
  I2C
  Relay
  USB
  VCC
  SCL
  SDA
  GND
  pos
  neg
  serLCD
