# Fritzing sketch pcb005 (saved by Fritzing 0.9.9b)
circuit board: 4.19286cm x 4.97139cm
breadboards: 1

parts:
  AHT20 = female pin header, 4 pins [form="♀ (female)"]
  LCD = female pin header, 3 pins [form="♀ (female)"]
  R1 = Resistor [tolerance=±5% power=0.25 resistance=220 package=THT]
  LED1 = LED - 5mm [color="Red (633nm)" current=0.030 package="5 mm [THT]"]
  Relay = female pin header, 2 pins [form="♀ (female)"]
  J3 = female pin header, 5 pins [form="♀ (female)"]
  J4 = female pin header, 2 pins [form="♀ (female)"]  # not connected
  J5 = female pin header, 2 pins [form="♀ (female)"]
  Part1 = Arduino Pro Mini (5V)  # not connected
  USB_Breakout = female pin header, 5 pins [form="♀ (female)"]
  S1 = Toggle Switch [package=THT]
  R2 = Resistor [tolerance=±5% power=0.25 resistance=220 package=THT]
  J1 = female pin header, 4 pins [form="♀ (female)"]
  J2 = female pin header, 3 pins [form="♀ (female)"]
  openLog = female pin header, 5 pins [form="♀ (female)"]

nets:
  N1: AHT20.pin1, LCD.pin1, USB_Breakout.pin5, S1.L1, J2.pin3, openLog.pin4
  N2: AHT20.pin2, J5.pin1
  N3: AHT20.pin3, J5.pin2
  N4: LCD.pin2, J3.pin1
  N5: R1.Pin_0, Relay.pin1, J3.pin4
  N6: R1.Pin_1, LED1.anode
  N7: S1.COM, J1.pin4
  N8: S1.L2, R2.Pin_1
  N9: J1.pin1, openLog.pin3
  N10: J1.pin2, openLog.pin2
  N11: J1.pin3, openLog.pin1

notes:
  OpenLog
  CONTROL
  MONITOR
  MODE SWITCH
  GND
  VCC
  I2C
  SDA
  SCL
  LCD
  TX
  RELAY
  LED
  USB
